// Logisim project Tic-Tac-Toe.circ as structural Verilog: 1 circuit, main circuit main
module main (
);

  wire and_1_out, and_3_out, and_4_out, and_5_out, and_6_out, and_7_out, B1, B2, B3, B4, B5, B6, B7, B8, B9,
       cl, code, I_Osel, in_out, mem, move_selector_1_p6, nor_1_out, nor_2_out, not_1_out, not_2_out,
       not_3_out, not_5_out, not_6_out, rs_latch_1_q_prime, RST, transistor_1_out, undriven,
       win_loose_screen_1_computer, win_loose_screen_1_draw, win_loose_screen_1_player;
  wire [1:0] CurrInput;
  wire [2:0] PageNum;
  wire [3:0] controlled_buffer_2_out, controlled_buffer_12_out, controlled_buffer_13_out,
       pull_resistor_4_node, random_1_out, register_1_q, S1, S2, S3, S4, S5, S6, S7, S8, S9;
  wire [7:0] addr, Cdm8_in, Cdm8_out, cdm_8_1_pc, cdm_8_1_ps, cdm_8_1_r0, cdm_8_1_r1, cdm_8_1_r2, cdm_8_1_r3,
       cdm_8_1_sp, codeData, I_Odat, move_selector_1_p9, rom_1_data, rom_2_data, rom_3_data;
  wire [7:7] not_4_out;
  wire [8:0] _11, _12, _13, _14, _15, _21, _22, _23, _24, _25, _31, _32, _33, _34, _35, _41, _42, _43, _44,
       _45, _51, _52, _53, _54, _55, _61, _62, _63, _64, _65, _71, _72, _73, _74, _75, _81, _82, _83, _84,
       _85, _91, _92, _93, _94, _95;

  DotMatrix #(.matrixcols(9), .matrixrows(9)) dotmatrix_1 (
    .col0(_11), .col1(_12), .col2(_13), .col3(_14), .col4(_15), .col5(_14), .col6(_13), .col7(_12), .col8(_11));
  DotMatrix #(.matrixcols(9), .matrixrows(9)) dotmatrix_2 (
    .col0(_41), .col1(_42), .col2(_43), .col3(_44), .col4(_45), .col5(_44), .col6(_43), .col7(_42), .col8(_41));
  DotMatrix #(.matrixcols(9), .matrixrows(9)) dotmatrix_3 (
    .col0(_71), .col1(_72), .col2(_73), .col3(_74), .col4(_75), .col5(_74), .col6(_73), .col7(_72), .col8(_71));
  // Probe on cdm_8_1_r0
  Clock clock_1 (.out(cl));
  Demultiplexer #(.width(8)) demultiplexer_1 (
    .out1(I_Odat), .in(Cdm8_out), .sel(CurrInput[1]), .en(and_1_out));  // open: out0
  and and_1 (and_1_out, ~in_out, mem);  // AND_Gate
  Pull_Resistor pull_resistor_1 (.node(I_Odat));
  and and_2 (CurrInput[1], addr[4], addr[5], addr[6], addr[7]);
  // Probe on cdm_8_1_r1
  // Probe on cdm_8_1_r2
  // Probe on cdm_8_1_r3
  DotMatrix #(.matrixcols(9), .matrixrows(9)) dotmatrix_4 (
    .col0(_21), .col1(_22), .col2(_23), .col3(_24), .col4(_25), .col5(_24), .col6(_23), .col7(_22), .col8(_21));
  DotMatrix #(.matrixcols(9), .matrixrows(9)) dotmatrix_5 (
    .col0(_51), .col1(_52), .col2(_53), .col3(_54), .col4(_55), .col5(_54), .col6(_53), .col7(_52), .col8(_51));
  DotMatrix #(.matrixcols(9), .matrixrows(9)) dotmatrix_6 (
    .col0(_81), .col1(_82), .col2(_83), .col3(_84), .col4(_85), .col5(_84), .col6(_83), .col7(_82), .col8(_81));
  // Probe on cdm_8_1_pc
  // Probe on cdm_8_1_ps
  // Probe on cdm_8_1_sp
  Pull_Resistor pull_resistor_2 (.node(addr));
  DotMatrix #(.matrixcols(9), .matrixrows(9)) dotmatrix_7 (
    .col0(_31), .col1(_32), .col2(_33), .col3(_34), .col4(_35), .col5(_34), .col6(_33), .col7(_32), .col8(_31));
  DotMatrix #(.matrixcols(9), .matrixrows(9)) dotmatrix_8 (
    .col0(_61), .col1(_62), .col2(_63), .col3(_64), .col4(_65), .col5(_64), .col6(_63), .col7(_62), .col8(_61));
  DotMatrix #(.matrixcols(9), .matrixrows(9)) dotmatrix_9 (
    .col0(_91), .col1(_92), .col2(_93), .col3(_94), .col4(_95), .col5(_94), .col6(_93), .col7(_92), .col8(_91));
  Decoder #(.select(2), .disabled(0)) decoder_1 (
    .out0(code), .out3(I_Osel), .sel(CurrInput), .en(mem));  // open: out1, out2
  CdM_8 cdm_8_1 (
    .data_code_prime(CurrInput[0]), .R0(cdm_8_1_r0), .R1(cdm_8_1_r1), .mem(mem), .R2(cdm_8_1_r2),
    .load_st_prime(in_out), .R3(cdm_8_1_r3), .addr(addr), .PC(cdm_8_1_pc), .SP(cdm_8_1_sp),
    .data_out(Cdm8_out), .data_in(Cdm8_in), .page(PageNum), .PS(cdm_8_1_ps), .clk(cl), .rset(RST));  // open: IAck, IRQ, vector, shadow
  Multiplexer #(.width(8)) multiplexer_1 (
    .in0(codeData), .in1(I_Odat), .out(Cdm8_in), .sel(CurrInput[1]), .en(and_3_out));
  and and_3 (and_3_out, in_out, mem);
  PS_saver ps_saver_1 (.I_Odat(I_Odat), .out(I_Odat), .in_out(in_out), .I_O_Adr(addr[3:0]), .I_O_sel(I_Osel));
  SP_saver sp_saver_1 (.I_Odat(I_Odat), .out(I_Odat), .in_out(in_out), .I_O_Adr(addr[3:0]), .I_O_sel(I_Osel));
  Button button_1 (.out(B1));
  Button button_2 (.out(B4));
  Button button_3 (.out(B7));
  LED Player (.in(win_loose_screen_1_player));
  Win_loose_screen win_loose_screen_1 (
    .I_Odat(I_Odat), .player(win_loose_screen_1_player), .computer(win_loose_screen_1_computer),
    .in_out(in_out), .I_O_Adr(addr[3:0]), .I_O_sel(I_Osel), .Draw(win_loose_screen_1_draw), .I_Odat_2(I_Odat));
  Button button_4 (.out(B3));
  Button button_5 (.out(B2));
  Button button_6 (.out(B6));
  Button button_7 (.out(B5));
  Button button_8 (.out(B9));
  Button button_9 (.out(B8));
  LED Computer (.in(win_loose_screen_1_computer));
  LED Draw (.in(win_loose_screen_1_draw));
  Button Restart (.out(RST));
  ROM rom_1 (.addr(addr), .data(rom_1_data), .sel(code));
  ROM rom_2 (.addr(addr), .data(rom_2_data), .sel(code));
  ROM rom_3 (.addr(addr), .data(rom_3_data), .sel(code));
  // Move_Selector move_selector_1: pin names not known; wires that end beside it: cl, S1, S2, S3, S4, move_selector_1_p6, move_selector_1_p6, S5, move_selector_1_p9, S6, S7, S8, S9
  Multiplexer #(.select(2), .width(8), .disabled(0), .enable("false")) multiplexer_2 (
    .in0(rom_1_data), .in1(rom_2_data), .in2(rom_3_data), .out(codeData), .sel(PageNum[1:0]));  // open: in3
  // Probe on move_selector_1_p9
  and and_4 (and_4_out, I_Osel, addr[0], addr[1], ~addr[2], addr[3], in_out);  // AND_Gate
  assign I_Odat = and_4_out ? move_selector_1_p9 : 8'bz;  // Controlled_Buffer controlled_buffer_1
  assign controlled_buffer_2_out = B1 ? 4'b0001 : 4'bz;  // Controlled_Buffer controlled_buffer_2
  not not_1 (not_1_out, transistor_1_out);
  DisplayReg1 displayreg1_1 (
    .in_out(in_out), .I_Odat(I_Odat[3:0]), .value(S1), .I_Oadr(addr[3:0]), .I_Osel(I_Osel), .out(I_Odat[3:0]));
  Transistor #(.\type ("n")) transistor_1 (.in(1'b0), .out(transistor_1_out), .gate(B2));
  Transistor #(.\type ("n")) transistor_2 (.in(1'b0), .out(transistor_1_out), .gate(B1));
  assign controlled_buffer_2_out = B3 ? 4'b0011 : 4'bz;  // Controlled_Buffer controlled_buffer_3
  assign controlled_buffer_2_out = B2 ? 4'b0010 : 4'bz;  // Controlled_Buffer controlled_buffer_4
  not not_2 (not_2_out, not_1_out);
  not not_3 (not_3_out, and_7_out);
  DisplayReg2 displayreg2_1 (
    .in_out(in_out), .I_Odat(I_Odat[3:0]), .value(S2), .I_Oadr(addr[3:0]), .I_Osel(I_Osel), .out(I_Odat[3:0]));
  DisplayReg3 displayreg3_1 (
    .in_out(in_out), .I_Odat(I_Odat[3:0]), .value(S3), .I_Oadr(addr[3:0]), .I_Osel(I_Osel), .out(I_Odat[3:0]));
  Transistor #(.\type ("n")) transistor_3 (.in(1'b0), .out(transistor_1_out), .gate(B3));
  Transistor #(.\type ("n")) transistor_4 (.in(1'b0), .out(transistor_1_out), .gate(B4));
  assign controlled_buffer_2_out = B5 ? 4'b0101 : 4'bz;  // Controlled_Buffer controlled_buffer_5
  assign controlled_buffer_2_out = B4 ? 4'b0100 : 4'bz;  // Controlled_Buffer controlled_buffer_6
  nor nor_1 (nor_1_out, not_1_out, not_2_out);
  nor nor_2 (nor_2_out, and_7_out, not_3_out);
  DisplayReg4 displayreg4_1 (
    .in_out(in_out), .I_Odat(I_Odat[3:0]), .value(S4), .I_Oadr(addr[3:0]), .I_Osel(I_Osel), .out(I_Odat[3:0]));
  DisplayControl displaycontrol_1 (.\input (S1), .outSignals_1_2({_12, _11}), .outSignals_3_4_5({_15, _14, _13}));
  DisplayControl displaycontrol_2 (.\input (S2), .outSignals_1_2({_22, _21}), .outSignals_3_4_5({_25, _24, _23}));
  DisplayControl displaycontrol_3 (.\input (S3), .outSignals_1_2({_32, _31}), .outSignals_3_4_5({_35, _34, _33}));
  Transistor #(.\type ("n")) transistor_5 (.in(1'b0), .out(transistor_1_out), .gate(B6));
  Transistor #(.\type ("n")) transistor_6 (.in(1'b0), .out(transistor_1_out), .gate(B5));
  assign controlled_buffer_2_out = B6 ? 4'b0110 : 4'bz;  // Controlled_Buffer controlled_buffer_7
  assign controlled_buffer_2_out = B7 ? 4'b0111 : 4'bz;  // Controlled_Buffer controlled_buffer_8
  RS_latch rs_latch_1 (.S(nor_1_out), .R(nor_2_out), .Q_prime(rs_latch_1_q_prime));  // open: Q, reset
  not not_4 (not_4_out[7], rs_latch_1_q_prime);
  DisplayReg5 displayreg5_1 (
    .in_out(in_out), .I_Odat(I_Odat[3:0]), .value(S5), .I_Oadr(addr[3:0]), .I_Osel(I_Osel), .out(I_Odat[3:0]));
  DisplayControl displaycontrol_4 (.\input (S6), .outSignals_1_2({_62, _61}), .outSignals_3_4_5({_65, _64, _63}));
  DisplayControl displaycontrol_5 (.\input (S5), .outSignals_1_2({_52, _51}), .outSignals_3_4_5({_55, _54, _53}));
  DisplayControl displaycontrol_6 (.\input (S4), .outSignals_1_2({_42, _41}), .outSignals_3_4_5({_45, _44, _43}));
  Transistor #(.\type ("n")) transistor_7 (.in(1'b0), .out(transistor_1_out), .gate(B7));
  Transistor #(.\type ("n")) transistor_8 (.in(1'b0), .out(transistor_1_out), .gate(B8));
  assign controlled_buffer_2_out = B8 ? 4'b1000 : 4'bz;  // Controlled_Buffer controlled_buffer_9
  assign controlled_buffer_2_out = B9 ? 4'b1001 : 4'bz;  // Controlled_Buffer controlled_buffer_10
  DisplayReg6 displayreg6_1 (
    .in_out(in_out), .I_Odat(I_Odat[3:0]), .value(S6), .I_Oadr(addr[3:0]), .I_Osel(I_Osel), .out(I_Odat[3:0]));
  DisplayReg7 displayreg7_1 (
    .in_out(in_out), .I_Odat(I_Odat[3:0]), .value(S7), .I_Oadr(addr[3:0]), .I_Osel(I_Osel), .out(I_Odat[3:0]));
  DisplayControl displaycontrol_7 (.\input (S8), .outSignals_1_2({_82, _81}), .outSignals_3_4_5({_85, _84, _83}));
  DisplayControl displaycontrol_8 (.\input (S7), .outSignals_1_2({_72, _71}), .outSignals_3_4_5({_75, _74, _73}));
  not not_5 (not_5_out, transistor_1_out);
  Pull_Resistor #(.pull(1)) pull_resistor_3 (.node(transistor_1_out));
  Transistor #(.\type ("n")) transistor_9 (.in(1'b0), .out(transistor_1_out), .gate(B9));
  DisplayReg8 displayreg8_1 (
    .in_out(in_out), .I_Odat(I_Odat[3:0]), .value(S8), .I_Oadr(addr[3:0]), .I_Osel(I_Osel), .out(I_Odat[3:0]));
  DisplayControl displaycontrol_9 (.\input (S9), .outSignals_1_2({_92, _91}), .outSignals_3_4_5({_95, _94, _93}));
  not not_6 (not_6_out, not_5_out);
  Register #(.width(4), .trigger("falling")) register_1 (
    .D(controlled_buffer_2_out), .Q(register_1_q), .clk(not_6_out));  // open: en, clr
  Pull_Resistor pull_resistor_4 (.node(pull_resistor_4_node));
  DisplayReg9 displayreg9_1 (
    .in_out(in_out), .I_Odat(I_Odat[3:0]), .value(S9), .I_Oadr(addr[3:0]), .I_Osel(I_Osel), .out(I_Odat[3:0]));
  and and_5 (and_5_out, I_Osel, addr[0], addr[1], ~addr[2], addr[3], in_out);  // AND_Gate
  Random #(.width(4), .seed(123)) random_1 (.clk(cl), .out(random_1_out));  // open: next, clr
  assign I_Odat = and_7_out ? {{4{not_4_out[7]}}, register_1_q} : 8'bz;  // Controlled_Buffer controlled_buffer_11
  assign controlled_buffer_12_out = undriven ? random_1_out : 4'bz;  // Controlled_Buffer controlled_buffer_12
  assign controlled_buffer_13_out = undriven ? 4'b0000 : 4'bz;  // Controlled_Buffer controlled_buffer_13
  and and_6 (and_6_out, ~addr[0], addr[1], ~addr[2], addr[3], I_Osel);  // AND_Gate
  and and_7 (and_7_out, and_6_out, in_out);

  // Other names for the same wires on the sheet: I_OData[7:0] = I_Odat; I_Oadr[3:0] = addr[3:0];
  //   I_OSet = CurrInput[1]; rd_rw = in_out

  // Notes on the sheet:
  //   ROM0 (main program)
  //   ROM1 (X-Win arbiter)
  //   ROM2 (0-Win arbiter)
  //   contents of rom_1 (hex, n*v repeats v):
  //   d0 f0 d1 ff 8c a2 74 ec 4 d0 fa b1 5 e5 b b7 f e1 9 d2 3 a6 db 10 d0 fb b2 d3 f9 7e e4 18 d3 f0 7e
  //   e0 18 bb f e1 18 d3 2 ab db 20 ee 9 d4
  //   contents of rom_2 (hex, n*v repeats v):
  //   d0 f1 b1 d2 3 d3 30 79 e1 40 d0 f2 b1 79 e1 1c d0 f3 b1 79 e1 1c d0 fc a2 d0 ff a3 d0 f4 b1 79 e1 2e
  //   d0 f7 b1 79 e1 2e d0 fc a2 d0 ff a3 d0 f5 b1 79 e1 40 d0 f9 b1 79 e1 40 d0 fc a2 d0 ff a3 d0 f5 b1
  //   79 e1 7c d0 f3 b1 79 e1 58 d0 f7 b1 79 e1 58 d0 fc a2 d0 ff a3 d0 f2 b1 79 e1 6a d0 f8 b1 79 e1 6a
  //   d0 fc a2 d0 ff a3 d0 f4 b1 79 e1 7c d0 f6 b1 79 e1 7c d0 fc a2 d0 ff a3 d0 f9 b1 79 e1 a6 d0 f3 b1
  //   79 e1 94 d0 f6 b1 79 e1 94 d0 fc a2 d0 ff a3 d0 f7 b1 79 e1 a6 d0 f8 b1 79 e1 a6 d0 fc a2 d0 ff a3
  //   d0 f1 b1 5 ed e0 8c b1 5 ed e0 8c b1 5 ed e0 8c b1 5 ed e0 8c b1 5 ed e0 8c b1 5 ed e0 8c b1 5 ed e0
  //   8c b1 5 ed e0 8c b1 5 ed e0 d0 fc b1 5 e1 e0 d2 1 a2 d0 ff a3 d9
  //   contents of rom_3 (hex, n*v repeats v):
  //   d0 f1 b1 d2 2 d3 30 79 e1 40 d0 f2 b1 79 e1 1c d0 f3 b1 79 e1 1c d0 fc a2 d0 ff a3 d0 f4 b1 79 e1 2e
  //   d0 f7 b1 79 e1 2e d0 fc a2 d0 ff a3 d0 f5 b1 79 e1 40 d0 f9 b1 79 e1 40 d0 fc a2 d0 ff a3 d0 f5 b1
  //   79 e1 7c d0 f3 b1 79 e1 58 d0 f7 b1 79 e1 58 d0 fc a2 d0 ff a3 d0 f2 b1 79 e1 6a d0 f8 b1 79 e1 6a
  //   d0 fc a2 d0 ff a3 d0 f4 b1 79 e1 7c d0 f6 b1 79 e1 7c d0 fc a2 d0 ff a3 d0 f9 b1 79 e1 a6 d0 f3 b1
  //   79 e1 94 d0 f6 b1 79 e1 94 d0 fc a2 d0 ff a3 d0 f7 b1 79 e1 a6 d0 f8 b1 79 e1 a6 d0 fc a2 d0 ff a3
  //   d9
  //   I/O Adr: 11111100
  //   I/O Adr: 11111011
  //   Input controller
  //   2
  //   3
  //   1
  //   5
  //   6
  //   4
  //   Random generator
  //   I/O Adr: 11111011
  //   I/O Adr: 11111010
  //   7
  //   8
  //   9
  //   Screen data setters
  //   Screen choosers
endmodule
