// Logisim project Tic-Tac-Toe_Modules.circ as structural Verilog: 14 circuits, main circuit DisplayReg1
module DisplayControl (
  input  [3:0] \input ,
  output [17:0] outSignals_1_2,
  output [26:0] outSignals_3_4_5
);

  Multiplexer #(.width(18), .disabled(0)) multiplexer_1 (
    .in0(18'h202fe), .in1(18'h10501), .out(outSignals_1_2), .sel(\input [0]), .en(\input [1]));
  Pull_Resistor pull_resistor_1 (.node(outSignals_1_2));
  Multiplexer #(.width(27), .disabled(0)) multiplexer_2 (
    .in0(27'h4060301), .in1(27'h405044), .out(outSignals_3_4_5), .sel(\input [0]), .en(\input [1]));
  Pull_Resistor pull_resistor_2 (.node(outSignals_3_4_5));
endmodule

module DisplayReg1 (
  input  I_Osel,
  input  [3:0] I_Oadr,
  input  in_out,
  input  [3:0] I_Odat,
  output [3:0] out,
  output [3:0] value
);

  wire and_1_out, decoder_1_out0, decoder_1_out1;

  Register #(.width(4)) register_1 (.D(I_Odat), .Q(value), .clk(decoder_1_out0));  // open: en, clr
  assign out = decoder_1_out1 ? value : 4'bz;  // Controlled_Buffer controlled_buffer_1
  and and_1 (and_1_out, ~I_Oadr[3], ~I_Oadr[2], ~I_Oadr[1], I_Oadr[0], I_Osel);  // AND_Gate
  Decoder #(.disabled(0)) decoder_1 (.out0(decoder_1_out0), .out1(decoder_1_out1), .sel(in_out), .en(and_1_out));
endmodule

module DisplayReg2 (
  input  I_Osel,
  input  [3:0] I_Oadr,
  input  in_out,
  input  [3:0] I_Odat,
  output [3:0] out,
  output [3:0] value
);

  wire and_1_out, decoder_1_out0, decoder_1_out1;

  Register #(.width(4)) register_1 (.D(I_Odat), .Q(value), .clk(decoder_1_out0));  // open: en, clr
  assign out = decoder_1_out1 ? value : 4'bz;  // Controlled_Buffer controlled_buffer_1
  and and_1 (and_1_out, ~I_Oadr[3], ~I_Oadr[2], I_Oadr[1], ~I_Oadr[0], I_Osel);  // AND_Gate
  Decoder #(.disabled(0)) decoder_1 (.out0(decoder_1_out0), .out1(decoder_1_out1), .sel(in_out), .en(and_1_out));
endmodule

module DisplayReg3 (
  input  I_Osel,
  input  [3:0] I_Oadr,
  input  in_out,
  input  [3:0] I_Odat,
  output [3:0] out,
  output [3:0] value
);

  wire and_1_out, decoder_1_out0, decoder_1_out1;

  Register #(.width(4)) register_1 (.D(I_Odat), .Q(value), .clk(decoder_1_out0));  // open: en, clr
  assign out = decoder_1_out1 ? value : 4'bz;  // Controlled_Buffer controlled_buffer_1
  and and_1 (and_1_out, ~I_Oadr[3], ~I_Oadr[2], I_Oadr[1], I_Oadr[0], I_Osel);  // AND_Gate
  Decoder #(.disabled(0)) decoder_1 (.out0(decoder_1_out0), .out1(decoder_1_out1), .sel(in_out), .en(and_1_out));
endmodule

module DisplayReg4 (
  input  I_Osel,
  input  [3:0] I_Oadr,
  input  in_out,
  input  [3:0] I_Odat,
  output [3:0] out,
  output [3:0] value
);

  wire and_1_out, decoder_1_out0, decoder_1_out1;

  Register #(.width(4)) register_1 (.D(I_Odat), .Q(value), .clk(decoder_1_out0));  // open: en, clr
  assign out = decoder_1_out1 ? value : 4'bz;  // Controlled_Buffer controlled_buffer_1
  and and_1 (and_1_out, ~I_Oadr[3], I_Oadr[2], ~I_Oadr[1], ~I_Oadr[0], I_Osel);  // AND_Gate
  Decoder #(.disabled(0)) decoder_1 (.out0(decoder_1_out0), .out1(decoder_1_out1), .sel(in_out), .en(and_1_out));
endmodule

module DisplayReg5 (
  input  I_Osel,
  input  [3:0] I_Oadr,
  input  in_out,
  input  [3:0] I_Odat,
  output [3:0] out,
  output [3:0] value
);

  wire and_1_out, decoder_1_out0, decoder_1_out1;

  Register #(.width(4)) register_1 (.D(I_Odat), .Q(value), .clk(decoder_1_out0));  // open: en, clr
  assign out = decoder_1_out1 ? value : 4'bz;  // Controlled_Buffer controlled_buffer_1
  and and_1 (and_1_out, ~I_Oadr[3], I_Oadr[2], ~I_Oadr[1], I_Oadr[0], I_Osel);  // AND_Gate
  Decoder #(.disabled(0)) decoder_1 (.out0(decoder_1_out0), .out1(decoder_1_out1), .sel(in_out), .en(and_1_out));
endmodule

module DisplayReg6 (
  input  I_Osel,
  input  [3:0] I_Oadr,
  input  in_out,
  input  [3:0] I_Odat,
  output [3:0] out,
  output [3:0] value
);

  wire and_1_out, decoder_1_out0, decoder_1_out1;

  Register #(.width(4)) register_1 (.D(I_Odat), .Q(value), .clk(decoder_1_out0));  // open: en, clr
  assign out = decoder_1_out1 ? value : 4'bz;  // Controlled_Buffer controlled_buffer_1
  and and_1 (and_1_out, ~I_Oadr[3], I_Oadr[2], I_Oadr[1], ~I_Oadr[0], I_Osel);  // AND_Gate
  Decoder #(.disabled(0)) decoder_1 (.out0(decoder_1_out0), .out1(decoder_1_out1), .sel(in_out), .en(and_1_out));
endmodule

module DisplayReg7 (
  input  I_Osel,
  input  [3:0] I_Oadr,
  input  in_out,
  input  [3:0] I_Odat,
  output [3:0] out,
  output [3:0] value
);

  wire and_1_out, decoder_1_out0, decoder_1_out1;

  Register #(.width(4)) register_1 (.D(I_Odat), .Q(value), .clk(decoder_1_out0));  // open: en, clr
  assign out = decoder_1_out1 ? value : 4'bz;  // Controlled_Buffer controlled_buffer_1
  and and_1 (and_1_out, ~I_Oadr[3], I_Oadr[2], I_Oadr[1], I_Oadr[0], I_Osel);  // AND_Gate
  Decoder #(.disabled(0)) decoder_1 (.out0(decoder_1_out0), .out1(decoder_1_out1), .sel(in_out), .en(and_1_out));
endmodule

module DisplayReg8 (
  input  I_Osel,
  input  [3:0] I_Oadr,
  input  in_out,
  input  [3:0] I_Odat,
  output [3:0] out,
  output [3:0] value
);

  wire and_1_out, decoder_1_out0, decoder_1_out1;

  Register #(.width(4)) register_1 (.D(I_Odat), .Q(value), .clk(decoder_1_out0));  // open: en, clr
  assign out = decoder_1_out1 ? value : 4'bz;  // Controlled_Buffer controlled_buffer_1
  and and_1 (and_1_out, I_Oadr[3], ~I_Oadr[2], ~I_Oadr[1], ~I_Oadr[0], I_Osel);  // AND_Gate
  Decoder #(.disabled(0)) decoder_1 (.out0(decoder_1_out0), .out1(decoder_1_out1), .sel(in_out), .en(and_1_out));
endmodule

module DisplayReg9 (
  input  I_Osel,
  input  [3:0] I_Oadr,
  input  in_out,
  input  [3:0] I_Odat,
  output [3:0] out,
  output [3:0] value
);

  wire and_1_out, decoder_1_out0, decoder_1_out1;

  Register #(.width(4)) register_1 (.D(I_Odat), .Q(value), .clk(decoder_1_out0));  // open: en, clr
  assign out = decoder_1_out1 ? value : 4'bz;  // Controlled_Buffer controlled_buffer_1
  and and_1 (and_1_out, I_Oadr[3], ~I_Oadr[2], ~I_Oadr[1], I_Oadr[0], I_Osel);  // AND_Gate
  Decoder #(.disabled(0)) decoder_1 (.out0(decoder_1_out0), .out1(decoder_1_out1), .sel(in_out), .en(and_1_out));
endmodule

module PS_saver (
  input  I_O_sel,
  input  [3:0] I_O_Adr,
  input  in_out,
  input  [7:0] I_Odat,
  output [7:0] out
);

  wire and_1_out, decoder_1_out0, decoder_1_out1;
  wire [7:0] register_1_q;

  Register register_1 (.D(I_Odat), .Q(register_1_q), .clk(decoder_1_out0));  // open: en, clr
  assign out = decoder_1_out1 ? register_1_q : 8'bz;  // Controlled_Buffer controlled_buffer_1
  and and_1 (and_1_out, I_O_Adr[3], I_O_Adr[2], I_O_Adr[1], I_O_Adr[0], I_O_sel);
  Decoder #(.disabled(0)) decoder_1 (.out0(decoder_1_out0), .out1(decoder_1_out1), .sel(in_out), .en(and_1_out));
endmodule

module SP_saver (
  input  I_O_sel,
  input  [3:0] I_O_Adr,
  input  in_out,
  input  [7:0] I_Odat,
  output [7:0] out
);

  wire and_1_out, decoder_1_out0, decoder_1_out1;
  wire [7:0] register_1_q;

  Register register_1 (.D(I_Odat), .Q(register_1_q), .clk(decoder_1_out0));  // open: en, clr
  assign out = decoder_1_out1 ? register_1_q : 8'bz;  // Controlled_Buffer controlled_buffer_1
  and and_1 (and_1_out, I_O_Adr[3], I_O_Adr[2], I_O_Adr[1], ~I_O_Adr[0], I_O_sel);  // AND_Gate
  Decoder #(.disabled(0)) decoder_1 (.out0(decoder_1_out0), .out1(decoder_1_out1), .sel(in_out), .en(and_1_out));
endmodule

module Win_loose_screen (
  input  I_O_sel,
  input  [3:0] I_O_Adr,
  input  in_out,
  input  [7:0] I_Odat,
  output player,
  output Draw,
  output computer,
  output [7:0] I_Odat_2
);

  wire and_4_out, decoder_1_out0, decoder_1_out1;
  wire [7:0] register_1_q;

  and and_1 (player, register_1_q[0], register_1_q[1]);
  and and_2 (Draw, register_1_q[0], ~register_1_q[1]);  // AND_Gate
  and and_3 (computer, ~register_1_q[0], register_1_q[1]);  // AND_Gate
  assign I_Odat_2 = decoder_1_out1 ? register_1_q : 8'bz;  // Controlled_Buffer controlled_buffer_1
  Decoder #(.disabled(0)) decoder_1 (.out0(decoder_1_out0), .out1(decoder_1_out1), .sel(in_out), .en(and_4_out));
  Register register_1 (.D(I_Odat), .Q(register_1_q), .clk(decoder_1_out0));  // open: en, clr
  and and_4 (and_4_out, I_O_Adr[3], I_O_Adr[2], ~I_O_Adr[1], ~I_O_Adr[0], I_O_sel);  // AND_Gate

  // Notes on the sheet:
  //   Page number
endmodule

module Move_Selector (
  input  [3:0] S1,
  input  [3:0] S2,
  input  [3:0] S3,
  input  [3:0] S4,
  input  [3:0] S5,
  input  [3:0] S6,
  input  [3:0] S7,
  input  [3:0] S8,
  input  [3:0] S9,
  input  CL,
  output [7:0] Move
);

  wire and_3_out, and_4_out, and_5_out, and_6_out, and_7_out, and_8_out, and_11_out, and_12_out, and_13_out,
       and_14_out, and_15_out, and_16_out, and_17_out, and_18_out, and_19_out, and_20_out, and_21_out,
       and_22_out, and_23_out, and_24_out, and_25_out, and_30_out, and_31_out, and_32_out, and_33_out,
       and_34_out, and_35_out, and_38_out, and_39_out, and_40_out, and_41_out, and_42_out, and_43_out,
       and_46_out, and_47_out, and_48_out, and_49_out, and_50_out, and_51_out, and_52_out, and_53_out,
       and_54_out, and_55_out, and_56_out, and_57_out, and_58_out, and_59_out, and_60_out, and_63_out,
       and_64_out, and_65_out, and_66_out, and_67_out, and_68_out, and_71_out, and_72_out, and_73_out,
       and_74_out, and_77_out, and_78_out, and_79_out, and_80_out, and_81_out, and_82_out, and_83_out,
       and_84_out, and_85_out, and_86_out, and_87_out, and_88_out, and_89_out, and_90_out, and_91_out,
       and_92_out, and_93_out, and_94_out, and_95_out, and_96_out, and_97_out, and_98_out, and_99_out,
       and_100_out, and_101_out, and_102_out, and_103_out, and_104_out, and_105_out, and_106_out,
       and_107_out, and_108_out, and_109_out, and_110_out, and_111_out, and_112_out, and_113_out,
       and_114_out, and_115_out, and_116_out, and_117_out, and_118_out, and_119_out, and_120_out,
       and_121_out, and_122_out, and_123_out, and_124_out, and_125_out, and_126_out, and_127_out,
       and_128_out, and_129_out, and_130_out, not_10_out, or_1_out, S1_0, S1_X, S1_Z, S2_0, S2_X, S2_Z, S3_0,
       S3_X, S3_Z, S4_0, S4_X, S4_Z, S5_0, S5_X, S5_Z, S6_0, S6_X, S6_Z, S7_0, S7_X, S7_Z, S8_0, S8_X, S8_Z,
       S9_0, S9_X, S9_Z;
  wire [3:0] random_1_out;
  wire [7:0] Comb_0_1, Comb_0_2, Comb_0_3, Comb_0_4, Comb_0_5, Comb_0_6, Comb_0_7, Comb_0_8, Comb_0_OUT,
       Comb_X_1, Comb_X_2, Comb_X_3, Comb_X_4, Comb_X_5, Comb_X_6, Comb_X_7, Comb_X_8, Comb_X_OUT,
       controlled_buffer_66_out, controlled_buffer_76_out, controlled_buffer_86_out, Hardcoded_Move;

  and and_1 (S1_0, S1[1], ~S1[0]);  // AND_Gate
  and and_2 (S1_X, S1[1], S1[0]);
  not not_1 (S1_Z, S1[1]);
  and and_3 (and_3_out, S1_0, S2_0, S3_Z);
  assign Comb_0_1 = and_3_out ? 8'hf3 : 8'bz;  // Controlled_Buffer controlled_buffer_1
  and and_4 (and_4_out, S2_0, S5_0, S8_Z);
  assign Comb_0_4 = and_4_out ? 8'hf8 : 8'bz;  // Controlled_Buffer controlled_buffer_2
  and and_5 (and_5_out, S7_0, S8_0, S9_Z);
  assign Comb_0_7 = and_5_out ? 8'hf9 : 8'bz;  // Controlled_Buffer controlled_buffer_3
  and and_6 (and_6_out, S1_X, S2_X, S3_Z);
  assign Comb_X_1 = and_6_out ? 8'hf3 : 8'bz;  // Controlled_Buffer controlled_buffer_4
  and and_7 (and_7_out, S2_X, S5_X, S8_Z);
  assign Comb_X_4 = and_7_out ? 8'hf8 : 8'bz;  // Controlled_Buffer controlled_buffer_5
  and and_8 (and_8_out, S7_X, S8_X, S9_Z);
  assign Comb_X_7 = and_8_out ? 8'hf9 : 8'bz;  // Controlled_Buffer controlled_buffer_6
  and and_9 (S2_X, S2[1], S2[0]);
  and and_10 (S2_0, S2[1], ~S2[0]);  // AND_Gate
  not not_2 (S2_Z, S2[1]);
  and and_11 (and_11_out, S1_Z, S2_Z, S3_Z, S4_Z, S5_X, S6_Z, S7_Z, S8_Z, S9_Z);
  and and_12 (and_12_out, S1_Z, S2_Z, S3_Z, S4_X, S5_Z, S6_Z, S7_Z, S8_Z, S9_Z);
  and and_13 (and_13_out, S1_Z, S2_Z, S3_Z, S4_Z, S5_Z, S6_Z, S7_X, S8_Z, S9_Z);
  and and_14 (and_14_out, S1_X, S2_Z, S3_Z, S4_X, S5_0, S6_Z, S7_Z, S8_Z, S9_Z);
  and and_15 (and_15_out, S1_Z, S2_Z, S3_Z, S4_X, S5_0, S6_X, S7_Z, S8_Z, S9_Z);
  and and_16 (and_16_out, S1_Z, S2_Z, S3_X, S4_Z, S5_0, S6_Z, S7_Z, S8_Z, S9_X);
  and and_17 (and_17_out, S1_Z, S2_Z, S3_Z, S4_Z, S5_0, S6_X, S7_Z, S8_Z, S9_X);
  and and_18 (and_18_out, S1_0, S2_Z, S3_Z, S4_Z, S5_X, S6_Z, S7_Z, S8_X, S9_Z);
  and and_19 (and_19_out, S1_Z, S2_Z, S3_Z, S4_Z, S5_0, S6_X, S7_Z, S8_Z, S9_X);
  and and_20 (and_20_out, S1_0, S2_Z, S3_0);
  Pull_Resistor pull_resistor_1 (.node(Comb_0_1));
  and and_21 (and_21_out, S2_0, S5_Z, S8_0);
  Pull_Resistor pull_resistor_2 (.node(Comb_0_4));
  and and_22 (and_22_out, S7_0, S8_Z, S9_0);
  Pull_Resistor pull_resistor_3 (.node(Comb_0_7));
  and and_23 (and_23_out, S1_X, S2_Z, S3_X);
  Pull_Resistor pull_resistor_4 (.node(Comb_X_1));
  and and_24 (and_24_out, S2_X, S5_Z, S8_X);
  Pull_Resistor pull_resistor_5 (.node(Comb_X_4));
  and and_25 (and_25_out, S7_X, S8_Z, S9_X);
  Pull_Resistor pull_resistor_6 (.node(Comb_X_7));
  and and_26 (S3_X, S3[1], S3[0]);
  and and_27 (S3_0, S3[1], ~S3[0]);  // AND_Gate
  not not_3 (S3_Z, S3[1]);
  assign Hardcoded_Move = and_11_out ? 8'hf1 : 8'bz;  // Controlled_Buffer controlled_buffer_7
  assign Hardcoded_Move = and_12_out ? 8'hf5 : 8'bz;  // Controlled_Buffer controlled_buffer_8
  assign Hardcoded_Move = and_13_out ? 8'hf5 : 8'bz;  // Controlled_Buffer controlled_buffer_9
  assign Hardcoded_Move = and_14_out ? 8'hf7 : 8'bz;  // Controlled_Buffer controlled_buffer_10
  assign Hardcoded_Move = and_15_out ? 8'hf1 : 8'bz;  // Controlled_Buffer controlled_buffer_11
  assign Hardcoded_Move = and_16_out ? 8'hf6 : 8'bz;  // Controlled_Buffer controlled_buffer_12
  assign Hardcoded_Move = and_17_out ? 8'hf3 : 8'bz;  // Controlled_Buffer controlled_buffer_13
  assign Hardcoded_Move = and_18_out ? 8'hf2 : 8'bz;  // Controlled_Buffer controlled_buffer_14
  assign Hardcoded_Move = and_19_out ? 8'hf3 : 8'bz;  // Controlled_Buffer controlled_buffer_15
  assign Comb_0_1 = and_20_out ? 8'hf2 : 8'bz;  // Controlled_Buffer controlled_buffer_16
  assign Comb_0_4 = and_21_out ? 8'hf5 : 8'bz;  // Controlled_Buffer controlled_buffer_17
  assign Comb_0_7 = and_22_out ? 8'hf8 : 8'bz;  // Controlled_Buffer controlled_buffer_18
  assign Comb_X_1 = and_23_out ? 8'hf2 : 8'bz;  // Controlled_Buffer controlled_buffer_19
  assign Comb_X_4 = and_24_out ? 8'hf5 : 8'bz;  // Controlled_Buffer controlled_buffer_20
  assign Comb_X_7 = and_25_out ? 8'hf8 : 8'bz;  // Controlled_Buffer controlled_buffer_21
  and and_28 (S4_X, S4[1], S4[0]);
  and and_29 (S4_0, S4[1], ~S4[0]);  // AND_Gate
  not not_4 (S4_Z, S4[1]);
  and and_30 (and_30_out, S1_Z, S2_0, S3_0);
  assign Comb_0_1 = and_30_out ? 8'hf1 : 8'bz;  // Controlled_Buffer controlled_buffer_22
  and and_31 (and_31_out, S2_Z, S5_0, S8_0);
  assign Comb_0_4 = and_31_out ? 8'hf2 : 8'bz;  // Controlled_Buffer controlled_buffer_23
  and and_32 (and_32_out, S7_Z, S8_0, S9_0);
  assign Comb_0_7 = and_32_out ? 8'hf7 : 8'bz;  // Controlled_Buffer controlled_buffer_24
  and and_33 (and_33_out, S1_Z, S2_X, S3_X);
  assign Comb_X_1 = and_33_out ? 8'hf1 : 8'bz;  // Controlled_Buffer controlled_buffer_25
  and and_34 (and_34_out, S2_Z, S5_X, S8_X);
  assign Comb_X_4 = and_34_out ? 8'hf2 : 8'bz;  // Controlled_Buffer controlled_buffer_26
  and and_35 (and_35_out, S7_Z, S8_X, S9_X);
  assign Comb_X_7 = and_35_out ? 8'hf7 : 8'bz;  // Controlled_Buffer controlled_buffer_27
  and and_36 (S5_X, S5[1], S5[0]);
  and and_37 (S5_0, S5[1], ~S5[0]);  // AND_Gate
  not not_5 (S5_Z, S5[1]);
  and and_38 (and_38_out, S1_0, S4_0, S7_Z);
  assign Comb_0_2 = and_38_out ? 8'hf7 : 8'bz;  // Controlled_Buffer controlled_buffer_28
  Pull_Resistor pull_resistor_7 (.node(Comb_0_2));
  and and_39 (and_39_out, S4_0, S5_0, S6_Z);
  assign Comb_0_5 = and_39_out ? 8'hf6 : 8'bz;  // Controlled_Buffer controlled_buffer_29
  Pull_Resistor pull_resistor_8 (.node(Comb_0_5));
  and and_40 (and_40_out, S3_0, S5_0, S7_Z);
  assign Comb_0_8 = and_40_out ? 8'hf7 : 8'bz;  // Controlled_Buffer controlled_buffer_30
  Pull_Resistor pull_resistor_9 (.node(Comb_0_8));
  and and_41 (and_41_out, S1_X, S4_X, S7_Z);
  assign Comb_X_2 = and_41_out ? 8'hf7 : 8'bz;  // Controlled_Buffer controlled_buffer_31
  Pull_Resistor pull_resistor_10 (.node(Comb_X_2));
  and and_42 (and_42_out, S4_X, S5_X, S6_Z);
  assign Comb_X_5 = and_42_out ? 8'hf6 : 8'bz;  // Controlled_Buffer controlled_buffer_32
  Pull_Resistor pull_resistor_11 (.node(Comb_X_5));
  and and_43 (and_43_out, S3_X, S5_X, S7_Z);
  assign Comb_X_8 = and_43_out ? 8'hf7 : 8'bz;  // Controlled_Buffer controlled_buffer_33
  Pull_Resistor pull_resistor_12 (.node(Comb_X_8));
  and and_44 (S6_X, S6[1], S6[0]);
  and and_45 (S6_0, S6[1], ~S6[0]);  // AND_Gate
  not not_6 (S6_Z, S6[1]);
  and and_46 (and_46_out, S1_Z, S2_X, S3_Z, S4_Z, S5_Z, S6_Z, S7_Z, S8_Z, S9_Z);
  assign Hardcoded_Move = and_46_out ? 8'hf5 : 8'bz;  // Controlled_Buffer controlled_buffer_34
  assign Hardcoded_Move = and_47_out ? 8'hf5 : 8'bz;  // Controlled_Buffer controlled_buffer_35
  and and_47 (and_47_out, S1_Z, S2_Z, S3_Z, S4_Z, S5_Z, S6_X, S7_Z, S8_Z, S9_Z);
  and and_48 (and_48_out, S1_Z, S2_Z, S3_Z, S4_Z, S5_Z, S6_Z, S7_Z, S8_Z, S9_X);
  assign Hardcoded_Move = and_48_out ? 8'hf5 : 8'bz;  // Controlled_Buffer controlled_buffer_36
  assign Hardcoded_Move = and_49_out ? 8'hf1 : 8'bz;  // Controlled_Buffer controlled_buffer_37
  and and_49 (and_49_out, S1_Z, S2_X, S3_Z, S4_X, S5_0, S6_Z, S7_Z, S8_Z, S9_Z);
  and and_50 (and_50_out, S1_Z, S2_Z, S3_Z, S4_X, S5_0, S6_Z, S7_X, S8_Z, S9_Z);
  assign Hardcoded_Move = and_50_out ? 8'hf1 : 8'bz;  // Controlled_Buffer controlled_buffer_38
  assign Hardcoded_Move = and_51_out ? 8'hf9 : 8'bz;  // Controlled_Buffer controlled_buffer_39
  and and_51 (and_51_out, S1_Z, S2_Z, S3_Z, S4_Z, S5_0, S6_X, S7_X, S8_Z, S9_Z);
  and and_52 (and_52_out, S1_Z, S2_Z, S3_Z, S4_Z, S5_0, S6_Z, S7_X, S8_X, S9_Z);
  assign Hardcoded_Move = and_52_out ? 8'hf9 : 8'bz;  // Controlled_Buffer controlled_buffer_40
  assign Hardcoded_Move = and_53_out ? 8'hf4 : 8'bz;  // Controlled_Buffer controlled_buffer_41
  and and_53 (and_53_out, S1_0, S2_Z, S3_Z, S4_Z, S5_X, S6_Z, S7_Z, S8_Z, S9_X);
  and and_54 (and_54_out, S1_Z, S2_Z, S3_Z, S4_Z, S5_0, S6_Z, S7_X, S8_X, S9_Z);
  assign Hardcoded_Move = and_54_out ? 8'hf9 : 8'bz;  // Controlled_Buffer controlled_buffer_42
  and and_55 (and_55_out, S1_0, S4_Z, S7_0);
  assign Comb_0_2 = and_55_out ? 8'hf4 : 8'bz;  // Controlled_Buffer controlled_buffer_43
  and and_56 (and_56_out, S4_0, S5_Z, S6_0);
  assign Comb_0_5 = and_56_out ? 8'hf5 : 8'bz;  // Controlled_Buffer controlled_buffer_44
  and and_57 (and_57_out, S3_0, S5_Z, S7_0);
  assign Comb_0_8 = and_57_out ? 8'hf5 : 8'bz;  // Controlled_Buffer controlled_buffer_45
  and and_58 (and_58_out, S1_X, S4_Z, S7_X);
  assign Comb_X_2 = and_58_out ? 8'hf4 : 8'bz;  // Controlled_Buffer controlled_buffer_46
  and and_59 (and_59_out, S4_X, S5_Z, S6_X);
  assign Comb_X_5 = and_59_out ? 8'hf5 : 8'bz;  // Controlled_Buffer controlled_buffer_47
  and and_60 (and_60_out, S3_X, S5_Z, S9_X);
  assign Comb_X_8 = and_60_out ? 8'hf5 : 8'bz;  // Controlled_Buffer controlled_buffer_48
  and and_61 (S7_0, S7[1], ~S7[0]);  // AND_Gate
  and and_62 (S7_X, S7[1], S7[0]);
  not not_7 (S7_Z, S7[1]);
  and and_63 (and_63_out, S1_Z, S4_0, S7_0);
  assign Comb_0_2 = and_63_out ? 8'hf1 : 8'bz;  // Controlled_Buffer controlled_buffer_49
  and and_64 (and_64_out, S4_Z, S5_0, S6_0);
  assign Comb_0_5 = and_64_out ? 8'hf4 : 8'bz;  // Controlled_Buffer controlled_buffer_50
  and and_65 (and_65_out, S3_Z, S5_0, S7_0);
  assign Comb_0_8 = and_65_out ? 8'hf3 : 8'bz;  // Controlled_Buffer controlled_buffer_51
  and and_66 (and_66_out, S1_Z, S4_X, S7_X);
  assign Comb_X_2 = and_66_out ? 8'hf1 : 8'bz;  // Controlled_Buffer controlled_buffer_52
  and and_67 (and_67_out, S4_Z, S5_X, S6_X);
  assign Comb_X_5 = and_67_out ? 8'hf4 : 8'bz;  // Controlled_Buffer controlled_buffer_53
  and and_68 (and_68_out, S3_Z, S5_X, S9_X);
  assign Comb_X_8 = and_68_out ? 8'hf3 : 8'bz;  // Controlled_Buffer controlled_buffer_54
  and and_69 (S8_X, S8[1], S8[0]);
  and and_70 (S8_0, S8[1], ~S8[0]);  // AND_Gate
  not not_8 (S8_Z, S8[1]);
  and and_71 (and_71_out, S1_0, S5_0, S9_Z);
  assign Comb_0_3 = and_71_out ? 8'hf9 : 8'bz;  // Controlled_Buffer controlled_buffer_55
  and and_72 (and_72_out, S3_0, S6_0, S9_Z);
  assign Comb_0_6 = and_72_out ? 8'hf9 : 8'bz;  // Controlled_Buffer controlled_buffer_56
  and and_73 (and_73_out, S1_X, S5_X, S9_Z);
  assign Comb_X_3 = and_73_out ? 8'hf9 : 8'bz;  // Controlled_Buffer controlled_buffer_57
  and and_74 (and_74_out, S3_X, S6_X, S9_Z);
  assign Comb_X_6 = and_74_out ? 8'hf9 : 8'bz;  // Controlled_Buffer controlled_buffer_58
  and and_75 (S9_X, S9[1], S9[0]);
  and and_76 (S9_0, S9[1], ~S9[0]);  // AND_Gate
  not not_9 (S9_Z, S9[1]);
  and and_77 (and_77_out, S1_Z, S2_Z, S3_Z, S4_Z, S5_Z, S6_Z, S7_Z, S8_X, S9_Z);
  and and_78 (and_78_out, S1_X, S2_Z, S3_Z, S4_Z, S5_Z, S6_Z, S7_Z, S8_Z, S9_Z);
  and and_79 (and_79_out, S1_Z, S2_Z, S3_X, S4_Z, S5_Z, S6_Z, S7_Z, S8_Z, S9_Z);
  and and_80 (and_80_out, S1_Z, S2_Z, S3_X, S4_X, S5_0, S6_Z, S7_Z, S8_Z, S9_Z);
  and and_81 (and_81_out, S1_Z, S2_Z, S3_Z, S4_X, S5_0, S6_Z, S7_Z, S8_X, S9_Z);
  and and_82 (and_82_out, S1_Z, S2_Z, S3_Z, S4_Z, S5_0, S6_X, S7_Z, S8_X, S9_Z);
  and and_83 (and_83_out, S1_Z, S2_Z, S3_Z, S4_Z, S5_0, S6_Z, S7_X, S8_Z, S9_X);
  and and_84 (and_84_out, S1_Z, S2_Z, S3_Z, S4_Z, S5_0, S6_X, S7_Z, S8_X, S9_Z);
  and and_85 (and_85_out, S1_Z, S2_Z, S3_Z, S4_Z, S5_0, S6_Z, S7_X, S8_Z, S9_X);
  and and_86 (and_86_out, S1_0, S5_Z, S9_0);
  Pull_Resistor pull_resistor_13 (.node(Comb_0_3));
  and and_87 (and_87_out, S3_0, S6_Z, S9_0);
  Pull_Resistor pull_resistor_14 (.node(Comb_0_6));
  and and_88 (and_88_out, S1_X, S5_Z, S9_X);
  Pull_Resistor pull_resistor_15 (.node(Comb_X_3));
  and and_89 (and_89_out, S3_X, S6_Z, S9_X);
  Pull_Resistor pull_resistor_16 (.node(Comb_X_6));
  assign Hardcoded_Move = and_77_out ? 8'hf5 : 8'bz;  // Controlled_Buffer controlled_buffer_59
  assign Hardcoded_Move = and_78_out ? 8'hf5 : 8'bz;  // Controlled_Buffer controlled_buffer_60
  assign Hardcoded_Move = and_79_out ? 8'hf5 : 8'bz;  // Controlled_Buffer controlled_buffer_61
  assign Hardcoded_Move = and_80_out ? 8'hf1 : 8'bz;  // Controlled_Buffer controlled_buffer_62
  assign Hardcoded_Move = and_81_out ? 8'hf7 : 8'bz;  // Controlled_Buffer controlled_buffer_63
  assign Hardcoded_Move = and_82_out ? 8'hf9 : 8'bz;  // Controlled_Buffer controlled_buffer_64
  assign Hardcoded_Move = and_83_out ? 8'hf8 : 8'bz;  // Controlled_Buffer controlled_buffer_65
  assign controlled_buffer_66_out = and_84_out ? 8'hf9 : 8'bz;  // Controlled_Buffer controlled_buffer_66
  assign Hardcoded_Move = and_85_out ? 8'hf8 : 8'bz;  // Controlled_Buffer controlled_buffer_67
  assign Comb_0_3 = and_86_out ? 8'hf5 : 8'bz;  // Controlled_Buffer controlled_buffer_68
  assign Comb_0_6 = and_87_out ? 8'hf6 : 8'bz;  // Controlled_Buffer controlled_buffer_69
  assign Comb_X_3 = and_88_out ? 8'hf5 : 8'bz;  // Controlled_Buffer controlled_buffer_70
  assign Comb_X_6 = and_89_out ? 8'hf6 : 8'bz;  // Controlled_Buffer controlled_buffer_71
  Pull_Resistor pull_resistor_17 (.node(Hardcoded_Move));
  and and_90 (and_90_out, S1_Z, S5_0, S9_0);
  assign Comb_0_3 = and_90_out ? 8'hf1 : 8'bz;  // Controlled_Buffer controlled_buffer_72
  and and_91 (and_91_out, S3_Z, S6_0, S9_0);
  assign Comb_0_6 = and_91_out ? 8'hf3 : 8'bz;  // Controlled_Buffer controlled_buffer_73
  and and_92 (and_92_out, S1_Z, S5_X, S9_X);
  assign Comb_X_3 = and_92_out ? 8'hf1 : 8'bz;  // Controlled_Buffer controlled_buffer_74
  and and_93 (and_93_out, S3_Z, S6_X, S9_X);
  assign Comb_X_6 = and_93_out ? 8'hf3 : 8'bz;  // Controlled_Buffer controlled_buffer_75
  and and_94 (and_94_out, S1_Z, S2_Z, S3_Z, S4_X, S5_0, S6_Z, S7_Z, S8_Z, S9_X);
  assign controlled_buffer_76_out = and_94_out ? 8'hf7 : 8'bz;  // Controlled_Buffer controlled_buffer_76
  assign controlled_buffer_76_out = and_95_out ? 8'hf3 : 8'bz;  // Controlled_Buffer controlled_buffer_77
  and and_95 (and_95_out, S1_X, S2_Z, S3_Z, S4_Z, S5_0, S6_X, S7_Z, S8_Z, S9_Z);
  and and_96 (and_96_out, S1_X, S2_Z, S3_Z, S4_Z, S5_0, S6_Z, S7_Z, S8_Z, S9_X);
  assign Hardcoded_Move = and_96_out ? 8'hf4 : 8'bz;  // Controlled_Buffer controlled_buffer_78
  assign Hardcoded_Move = and_97_out ? 8'hf9 : 8'bz;  // Controlled_Buffer controlled_buffer_79
  and and_97 (and_97_out, S1_Z, S2_X, S3_Z, S4_Z, S5_0, S6_Z, S7_X, S8_Z, S9_Z);
  and and_98 (and_98_out, S1_Z, S2_Z, S3_X, S4_Z, S5_0, S6_X, S7_Z, S8_Z, S9_Z);
  assign Hardcoded_Move = and_98_out ? 8'hf9 : 8'bz;  // Controlled_Buffer controlled_buffer_80
  assign Hardcoded_Move = and_99_out ? 8'hf7 : 8'bz;  // Controlled_Buffer controlled_buffer_81
  and and_99 (and_99_out, S1_Z, S2_Z, S3_Z, S4_Z, S5_0, S6_Z, S7_Z, S8_X, S9_X);
  and and_100 (and_100_out, S1_0, S2_Z, S3_Z, S4_X, S5_X, S6_Z, S7_Z, S8_Z, S9_Z);
  assign Hardcoded_Move = and_100_out ? 8'hf6 : 8'bz;  // Controlled_Buffer controlled_buffer_82
  assign Comb_0_OUT = Comb_0_1[7] ? Comb_0_1 : 8'bz;  // Controlled_Buffer controlled_buffer_83
  and and_101 (and_101_out, ~Comb_0_1[7], Comb_0_2[7]);  // AND_Gate
  assign Comb_0_OUT = and_101_out ? Comb_0_2 : 8'bz;  // Controlled_Buffer controlled_buffer_84
  and and_102 (and_102_out, ~and_101_out, Comb_0_3[7]);  // AND_Gate
  and and_103 (and_103_out, ~and_102_out, Comb_0_4[7]);  // AND_Gate
  assign Comb_0_OUT = and_102_out ? Comb_0_3 : 8'bz;  // Controlled_Buffer controlled_buffer_85
  and and_104 (and_104_out, ~and_103_out, Comb_0_5[7]);  // AND_Gate
  and and_105 (and_105_out, S1_X, S2_X, S3_Z, S4_Z, S5_0, S6_Z, S7_Z, S8_Z, S9_Z);
  assign controlled_buffer_86_out = and_105_out ? 8'hf3 : 8'bz;  // Controlled_Buffer controlled_buffer_86
  assign controlled_buffer_86_out = and_106_out ? 8'hf2 : 8'bz;  // Controlled_Buffer controlled_buffer_87
  and and_106 (and_106_out, S1_X, S2_Z, S3_Z, S4_Z, S5_0, S6_Z, S7_X, S8_Z, S9_Z);
  and and_107 (and_107_out, S1_Z, S2_X, S3_X, S4_Z, S5_0, S6_Z, S7_Z, S8_Z, S9_Z);
  assign Hardcoded_Move = and_107_out ? 8'hf1 : 8'bz;  // Controlled_Buffer controlled_buffer_88
  assign Hardcoded_Move = and_108_out ? 8'hf1 : 8'bz;  // Controlled_Buffer controlled_buffer_89
  and and_108 (and_108_out, S1_Z, S2_X, S3_Z, S4_Z, S5_0, S6_Z, S7_Z, S8_X, S9_Z);
  and and_109 (and_109_out, S1_Z, S2_Z, S3_X, S4_Z, S5_0, S6_Z, S7_X, S8_Z, S9_Z);
  assign Hardcoded_Move = and_109_out ? 8'hf4 : 8'bz;  // Controlled_Buffer controlled_buffer_90
  assign Hardcoded_Move = and_110_out ? 8'hf8 : 8'bz;  // Controlled_Buffer controlled_buffer_91
  and and_110 (and_110_out, S1_0, S2_X, S3_Z, S4_Z, S5_X, S6_Z, S7_Z, S8_Z, S9_Z);
  and and_111 (and_111_out, S1_0, S2_Z, S3_Z, S4_Z, S5_X, S6_X, S7_Z, S8_Z, S9_Z);
  assign Hardcoded_Move = and_111_out ? 8'hf4 : 8'bz;  // Controlled_Buffer controlled_buffer_92
  assign Comb_0_OUT = and_103_out ? Comb_0_4 : 8'bz;  // Controlled_Buffer controlled_buffer_93
  assign Comb_0_OUT = and_104_out ? Comb_0_5 : 8'bz;  // Controlled_Buffer controlled_buffer_94
  and and_112 (and_112_out, ~and_104_out, Comb_0_6[7]);  // AND_Gate
  assign Comb_0_OUT = and_112_out ? Comb_0_6 : 8'bz;  // Controlled_Buffer controlled_buffer_95
  and and_113 (and_113_out, ~and_112_out, Comb_0_7[7]);  // AND_Gate
  and and_114 (and_114_out, ~and_113_out, Comb_0_8[7]);  // AND_Gate
  assign Comb_0_OUT = and_113_out ? Comb_0_7 : 8'bz;  // Controlled_Buffer controlled_buffer_96
  Pull_Resistor pull_resistor_18 (.node(Comb_0_OUT));
  Random #(.width(4), .seed(123)) random_1 (.clk(CL), .out(random_1_out));  // open: next, clr
  and and_115 (and_115_out, S1_X, S2_Z, S3_X, S4_Z, S5_0, S6_Z, S7_Z, S8_Z, S9_Z);
  assign Hardcoded_Move = and_115_out ? 8'hf2 : 8'bz;  // Controlled_Buffer controlled_buffer_97
  assign Hardcoded_Move = and_116_out ? 8'hf7 : 8'bz;  // Controlled_Buffer controlled_buffer_98
  and and_116 (and_116_out, S1_X, S2_Z, S3_Z, S4_Z, S5_0, S6_Z, S7_Z, S8_X, S9_Z);
  and and_117 (and_117_out, S1_Z, S2_X, S3_Z, S4_Z, S5_0, S6_X, S7_Z, S8_Z, S9_Z);
  assign Hardcoded_Move = and_117_out ? 8'hf3 : 8'bz;  // Controlled_Buffer controlled_buffer_99
  assign Hardcoded_Move = and_118_out ? 8'hf3 : 8'bz;  // Controlled_Buffer controlled_buffer_100
  and and_118 (and_118_out, S1_Z, S2_X, S3_Z, S4_Z, S5_0, S6_Z, S7_Z, S8_Z, S9_X);
  and and_119 (and_119_out, S1_Z, S2_Z, S3_X, S4_Z, S5_0, S6_Z, S7_Z, S8_X, S9_Z);
  assign Hardcoded_Move = and_119_out ? 8'hf9 : 8'bz;  // Controlled_Buffer controlled_buffer_101
  assign Hardcoded_Move = and_120_out ? 8'hf7 : 8'bz;  // Controlled_Buffer controlled_buffer_102
  and and_120 (and_120_out, S1_0, S2_Z, S3_X, S4_Z, S5_X, S6_Z, S7_Z, S8_Z, S9_Z);
  and and_121 (and_121_out, S1_0, S2_Z, S3_Z, S4_Z, S5_X, S6_Z, S7_X, S8_Z, S9_Z);
  assign Hardcoded_Move = and_121_out ? 8'hf3 : 8'bz;  // Controlled_Buffer controlled_buffer_103
  assign Comb_0_OUT = and_114_out ? Comb_0_8 : 8'bz;  // Controlled_Buffer controlled_buffer_104
  and and_122 (and_122_out, ~Comb_0_OUT[7], Comb_X_OUT[7]);  // AND_Gate
  assign Comb_X_OUT = and_125_out ? Comb_X_7 : 8'bz;  // Controlled_Buffer controlled_buffer_105
  assign Comb_X_OUT = and_124_out ? Comb_X_8 : 8'bz;  // Controlled_Buffer controlled_buffer_106
  Pull_Resistor pull_resistor_19 (.node(Comb_X_OUT));
  assign Move = Comb_0_OUT[7] ? Comb_0_OUT : 8'bz;  // Controlled_Buffer controlled_buffer_107
  assign Move = and_122_out ? Comb_X_OUT : 8'bz;  // Controlled_Buffer controlled_buffer_108
  and and_123 (and_123_out, ~and_122_out, Hardcoded_Move[7]);  // AND_Gate
  or or_1 (or_1_out, Comb_0_OUT[7], Comb_X_OUT[7], Hardcoded_Move[7]);
  not not_10 (not_10_out, or_1_out);
  assign Move = not_10_out ? {4'b1111, random_1_out} : 8'bz;  // Controlled_Buffer controlled_buffer_109
  assign Comb_X_OUT = and_127_out ? Comb_X_6 : 8'bz;  // Controlled_Buffer controlled_buffer_110
  and and_124 (and_124_out, ~and_125_out, Comb_X_8[7]);  // AND_Gate
  assign Move = and_123_out ? Hardcoded_Move : 8'bz;  // Controlled_Buffer controlled_buffer_111
  assign Comb_X_OUT = and_126_out ? Comb_X_5 : 8'bz;  // Controlled_Buffer controlled_buffer_112
  and and_125 (and_125_out, ~and_127_out, Comb_X_7[7]);  // AND_Gate
  assign Comb_X_OUT = and_128_out ? Comb_X_4 : 8'bz;  // Controlled_Buffer controlled_buffer_113
  and and_126 (and_126_out, ~and_128_out, Comb_X_5[7]);  // AND_Gate
  and and_127 (and_127_out, ~and_126_out, Comb_X_6[7]);  // AND_Gate
  assign Comb_X_OUT = and_129_out ? Comb_X_3 : 8'bz;  // Controlled_Buffer controlled_buffer_114
  and and_128 (and_128_out, ~and_129_out, Comb_X_4[7]);  // AND_Gate
  assign Comb_X_OUT = Comb_X_1[7] ? Comb_X_1 : 8'bz;  // Controlled_Buffer controlled_buffer_115
  assign Comb_X_OUT = and_130_out ? Comb_X_2 : 8'bz;  // Controlled_Buffer controlled_buffer_116
  and and_129 (and_129_out, ~and_130_out, Comb_X_3[7]);  // AND_Gate
  and and_130 (and_130_out, ~Comb_X_1[7], Comb_X_2[7]);  // AND_Gate

  // Notes on the sheet:
  //   00*
  //   ---
  //   ---
  //   -0-
  //   -0-
  //   -*-
  //   ---
  //   ---
  //   00*
  //   XX*
  //   ---
  //   ---
  //   -X-
  //   -X-
  //   -*-
  //   ---
  //   ---
  //   XX*
  //   *--
  //   -X-
  //   ---
  //   ---
  //   X*-
  //   ---
  //   ---
  //   -*-
  //   X--
  //   X--
  //   X0-
  //   *--
  //   *--
  //   X0X
  //   ---
  //   --X
  //   -0*
  //   --X
  //   --*
  //   -0X
  //   --X
  //   0*-
  //   -X-
  //   -X-
  //   --*
  //   -0X
  //   --X
  //   0*0
  //   ---
  //   ---
  //   -0-
  //   -*-
  //   -0-
  //   ---
  //   ---
  //   0*0
  //   X*X
  //   ---
  //   ---
  //   -X-
  //   -*-
  //   -X-
  //   ---
  //   ---
  //   X*X
  //   *00
  //   ---
  //   ---
  //   -*-
  //   -0-
  //   -0-
  //   ---
  //   ---
  //   *00
  //   *XX
  //   ---
  //   ---
  //   -*-
  //   -X-
  //   -X-
  //   ---
  //   ---
  //   *XX
  //   0--
  //   0--
  //   *--
  //   ---
  //   00*
  //   ---
  //   --0
  //   -0-
  //   *--
  //   X--
  //   X--
  //   *--
  //   ---
  //   XX*
  //   ---
  //   --X
  //   -X-
  //   *--
  //   -X-
  //   -*-
  //   ---
  //   ---
  //   -*X
  //   ---
  //   ---
  //   -*-
  //   --X
  //   *X-
  //   X0-
  //   ---
  //   *--
  //   X0-
  //   X--
  //   ---
  //   -0X
  //   X-*
  //   ---
  //   -0-
  //   XX*
  //   0--
  //   *X-
  //   --X
  //   ---
  //   -0-
  //   XX*
  //   0--
  //   *--
  //   0--
  //   ---
  //   0*0
  //   ---
  //   --0
  //   -*-
  //   0--
  //   X--
  //   *--
  //   X--
  //   ---
  //   X*X
  //   ---
  //   --X
  //   -*-
  //   X--
  //   *--
  //   0--
  //   0--
  //   ---
  //   *00
  //   ---
  //   --*
  //   -0-
  //   0--
  //   *--
  //   X--
  //   X--
  //   ---
  //   *XX
  //   ---
  //   --*
  //   -X-
  //   X--
  //   0--
  //   -0-
  //   --*
  //   --0
  //   --0
  //   --*
  //   X--
  //   -X-
  //   --*
  //   --X
  //   --X
  //   --*
  //   ---
  //   -*-
  //   -X-
  //   X--
  //   -*-
  //   ---
  //   --X
  //   -*-
  //   ---
  //   *-X
  //   X0-
  //   ---
  //   ---
  //   X0-
  //   *X-
  //   ---
  //   -0X
  //   -X*
  //   ---
  //   -0-
  //   X*X
  //   ---
  //   -0X
  //   -X*
  //   ---
  //   -0-
  //   X*X
  //   0--
  //   -*-
  //   --0
  //   --0
  //   --*
  //   --0
  //   X--
  //   -*-
  //   --X
  //   --X
  //   --*
  //   --X
  //   *--
  //   -0-
  //   --0
  //   --*
  //   --0
  //   --0
  //   *--
  //   -X-
  //   --X
  //   --*
  //   --X
  //   --X
  //   ---
  //   X0-
  //   *-X
  //   X-*
  //   -0X
  //   ---
  //   X--
  //   *0-
  //   --X
  //   -X-
  //   -0-
  //   X-*
  //   --X
  //   -0X
  //   --*
  //   ---
  //   -0-
  //   *XX
  //   0--
  //   XX*
  //   ---
  //   Hardcoded first or second move
  //   XX*
  //   -0-
  //   ---
  //   X--
  //   *0-
  //   X--
  //   *XX
  //   -0-
  //   ---
  //   *X-
  //   -0-
  //   -X-
  //   --X
  //   *0-
  //   X--
  //   0X-
  //   -X-
  //   -*-
  //   0--
  //   *XX
  //   ---
  //   X*X
  //   -0-
  //   ---
  //   X--
  //   -0-
  //   *X-
  //   -X*
  //   -0X
  //   ---
  //   -X*
  //   -0-
  //   --X
  //   --X
  //   -0-
  //   -X*
  //   0-X
  //   -X-
  //   *--
  //   0-*
  //   -X-
  //   X--
endmodule
